# Fritzing sketch TrafficLight (saved by Fritzing 0.9.3b)
breadboards: 1

parts:
  元件1 = Arduino Uno (Rev3)
  S1 = Pushbutton [package="[THT]"]
  S2 = Pushbutton [package="[THT]"]
  LED1 = LED - 5mm [color="Green (570nm)" package="5 mm [THT]"]
  R1 = Resistor [tolerance=±5% resistance=220 package=THT]
  R2 = Resistor [tolerance=±5% resistance=220 package=THT]
  R3 = Resistor [tolerance=±5% resistance=220 package=THT]
  LED2 = LED - 5mm [color="Yellow (595nm)" package="5 mm [THT]"]
  LED3 = LED - 5mm [color="Red (633nm)" package="5 mm [THT]"]
  R4 = Photocell (LDR) [package=THT]
  R5 = Resistor [tolerance=±5% resistance=10k package=THT]
  R6 = Resistor [tolerance=±5% resistance=220 package=THT]
  R7 = Resistor [tolerance=±5% resistance=220 package=THT]

nets:
  N1: 元件1.D11_PWM/MOSI, S2.Pin_1, S2.Pin_2
  N2: 元件1.D12/MISO, S1.Pin_1, S1.Pin_2
  N3: 元件1.D2, LED1.cathode
  N4: 元件1.D3_PWM, LED2.cathode
  N5: 元件1.D4, LED3.cathode
  N6: S1.Pin_3, S1.Pin_4, R7.Pin_1
  N7: S2.Pin_3, S2.Pin_4, R6.Pin_1
  N8: LED1.anode, R1.Pin_0
  N9: R1.Pin_1, R3.Pin_1, R5.Pin_1
  N10: R2.Pin_0, LED2.anode
  N11: R3.Pin_0, LED3.anode
  N12: R4.pin_1, R5.Pin_0
  N13: R6.Pin_0, R7.Pin_0
